# Fritzing sketch AutoLight (saved by Fritzing 0.8.7b)
circuit board: 16.9333cm x 5.64444cm

parts:
  R2 = Photocell (LDR) [package=THT]
  R3 = Resistor [tolerance=±5% resistance=220 package=THT]
  K1 = Relay [part_number=FRS1B-S package=THT]
  Arduino1 = Arduino Uno (Rev3)

nets:
  N1: R2.pin_0, R3.Pin_0
  N2: R2.pin_1, K1.C1, K1.C2, Arduino1.GND, Arduino1.D3_PWM
  N3: R3.Pin_1, Arduino1.A0
